# Fritzing sketch ledblinkWithButton (saved by Fritzing 0.9.2b)
breadboards: 1

parts:
  Composant1 = Arduino Uno (Rev3)
  LED2 = LED - 5mm [color="Red (633nm)" package="5 mm [THT]"]
  S1 = Pushbutton [package="[THT]"]

nets:
  N1: Composant1.D13/SCK, S1.Pin_3, S1.Pin_4
  N2: Composant1.GND, LED2.cathode
  N3: LED2.anode, S1.Pin_1, S1.Pin_2
