# Fritzing sketch ledblink2 (saved by Fritzing 0.9.2b)
breadboards: 1

parts:
  S1 = Pushbutton [package="[THT]"]
  Composant1 = Arduino Uno (Rev3)
  R1 = Resistor [tolerance=±5% resistance=220 package="0402 [SMD]"]
  LED1 = LED - 3mm [color="Red (633nm)" package="3 mm [THT]"]

nets:
  N1: S1.Pin_1, S1.Pin_2, Composant1.D2, R1.Pin_0
  N2: S1.Pin_3, S1.Pin_4, Composant1.5V
  N3: Composant1.D13/SCK, LED1.anode
  N4: Composant1.GND, R1.Pin_1, LED1.cathode
