# Fritzing sketch DistanceSynthesizer2 (saved by Fritzing 0.9.2b)
breadboards: 1

parts:
  Composant1 = SRF05 Ultrasonic Rangefinder
  Composant2 = Arduino Uno (Rev3)
  SP1 = SPEAKER [package=pcb_mount_speaker]
  R1 = Rotary Potentiometer (Small) [maximum_resistance=100kΩ package=THT]

nets:
  VCC: Composant1.VCC, Composant2.5V, R1.leg1
  N1: Composant1.Trig, Composant2.D2
  N2: Composant1.Echo, Composant2.D3_PWM
  GND: Composant1.GND, Composant2.GND, SP1.+, R1.leg2
  N3: Composant2.A0, R1.wiper
  N4: Composant2.D13/SCK, SP1.-
