# Fritzing sketch Love-o-meter-with-buzzer (saved by Fritzing 0.9.2b)
breadboards: 1

parts:
  Composant1 = Arduino Uno (Rev3)
  R1 = Resistor [tolerance=±5% resistance=220 package=THT]
  R2 = Resistor [tolerance=±5% resistance=220 package=THT]
  R3 = Resistor [tolerance=±5% resistance=220 package=THT]
  LED1 = LED - 5mm [color="Red (633nm)" package="5 mm [THT]"]
  LED2 = LED - 5mm [color="Green (570nm)" package="5 mm [THT]"]
  LED3 = LED - 5mm [color="Blue (525nm)" package="5 mm [THT]"]
  T1 = LM34 Temperature Sensor [package="TO92 [THT]"]
  J1 = Piezo Speaker

nets:
  N1: Composant1.A0, T1.Vout
  N2: Composant1.D2, LED3.anode
  N3: Composant1.D3_PWM, LED2.anode
  N4: Composant1.D4, LED1.anode
  N5: Composant1.D5_PWM, J1.pin2
  N6: Composant1.5V, T1.+Vs
  GND: Composant1.GND, R1.Pin_0, R2.Pin_0, R3.Pin_0, T1.GND, J1.pin1
  N7: R1.Pin_1, LED3.cathode
  N8: R2.Pin_1, LED2.cathode
  N9: R3.Pin_1, LED1.cathode
